// Logisim project CRC.circ as structural Verilog: 4 circuits, main circuit CRC
module CRC (
  input  [7:0] in_1,
  input  [3:0] in_2,
  output [10:0] out_3
);

  loop loop_1 (.in_1({in_1, 3'b000}), .in_2(in_2), .out_3(out_3[2:0]));

  assign out_3[10:3] = in_1;
endmodule

module mod2 (
  input  [3:0] A,
  input  [3:0] B,
  output out_3,
  output [2:0] out_4
);

  wire [3:0] multiplexer_1_out, xor_1_out;

  assign xor_1_out = A ^ B;  // XOR_Gate xor_1, 4 bits wide
  Multiplexer #(.width(4)) multiplexer_1 (.in0(A), .in1(xor_1_out), .out(multiplexer_1_out), .sel(A[3]));  // open: en
  Bit_Extender #(.in_width(4), .out_width(3)) bit_extender_1 (.in(multiplexer_1_out), .out(out_4));

  assign out_3 = A[3];
endmodule

module loop (
  input  [10:0] in_1,
  input  [3:0] in_2,
  output [2:0] out_3
);

  wire [2:0] mod2_1_out_4, mod2_2_out_4, mod2_3_out_4, mod2_4_out_4, mod2_6_out_4, mod2_7_out_4;
  wire [3:1] mod2_5_out_4;

  mod2 mod2_1 (.A(in_1[10:7]), .B(in_2), .out_4(mod2_1_out_4));  // open: out_3
  mod2 mod2_2 (.A({mod2_1_out_4, in_1[6]}), .B(in_2), .out_4(mod2_2_out_4));  // open: out_3
  mod2 mod2_3 (.A({mod2_2_out_4, in_1[5]}), .B(in_2), .out_4(mod2_3_out_4));  // open: out_3
  mod2 mod2_4 (.A({mod2_3_out_4, in_1[4]}), .B(in_2), .out_4(mod2_4_out_4));  // open: out_3
  mod2 mod2_5 (.A({mod2_4_out_4, in_1[3]}), .B(in_2), .out_4(mod2_5_out_4));  // open: out_3
  mod2 mod2_6 (.A({mod2_5_out_4, in_1[2]}), .B(in_2), .out_4(mod2_6_out_4));  // open: out_3
  mod2 mod2_7 (.A({mod2_6_out_4, in_1[1]}), .B(in_2), .out_4(mod2_7_out_4));  // open: out_3
  mod2 mod2_8 (.A({mod2_7_out_4, in_1[0]}), .B(in_2), .out_4(out_3));  // open: out_3
endmodule

module test (
  input  [7:0] in_1,
  input  [3:0] in_2,
  output [10:0] out_3
);

  CRC crc_1 (.in_1(in_1), .in_2(in_2), .out_3(out_3));
endmodule
