// Logisim project ftoi.circ as structural Verilog: 1 circuit, main circuit ftoi
module ftoi (
  input  [15:0] in_1,
  output [31:0] out_2
);

  wire comparator_1_eq, comparator_2_eq, comparator_3_lt, or_1_out, or_2_out;
  wire [4:0] subtractor_1_out;
  wire [10:0] bit_extender_1_out;
  wire [30:0] bit_extender_2_out, not_1_out, shifter_1_out, shifter_2_out;
  wire [31:0] adder_1_out, bit_extender_3_out, bit_extender_4_out, multiplexer_1_out;

  assign bit_extender_1_out = {{1{1'b1}}, in_1[9:0]};  // Bit_Extender bit_extender_1
  assign bit_extender_2_out = {{20{1'b0}}, bit_extender_1_out};  // Bit_Extender bit_extender_2
  Subtractor #(.width(5)) subtractor_1 (.a(in_1[14:10]), .b(5'b01111), .out(subtractor_1_out));  // open: bin, bout
  Shifter #(.width(31)) shifter_1 (.in(bit_extender_2_out), .\dist (subtractor_1_out), .out(shifter_1_out));
  Shifter #(.width(31), .shift("lr")) shifter_2 (.in(shifter_1_out), .\dist (5'b01010), .out(shifter_2_out));
  assign not_1_out = ~shifter_2_out;  // NOT_Gate not_1, 31 bits wide
  Comparator #(.width(5), .mode("unsigned")) comparator_1 (
    .a({5{1'b0}}), .b(in_1[14:10]), .eq(comparator_1_eq));  // open: gt, lt
  Comparator #(.width(5), .mode("unsigned")) comparator_2 (
    .a({5{1'b1}}), .b(in_1[14:10]), .eq(comparator_2_eq));  // open: gt, lt
  assign bit_extender_3_out = {{1{1'b1}}, not_1_out};  // Bit_Extender bit_extender_3
  or or_1 (or_1_out, comparator_1_eq, comparator_2_eq);
  Comparator #(.width(5)) comparator_3 (.a(subtractor_1_out), .b({5{1'b0}}), .lt(comparator_3_lt));  // open: gt, eq
  assign bit_extender_4_out = {{1{1'b0}}, shifter_2_out};  // Bit_Extender bit_extender_4
  or or_2 (or_2_out, or_1_out, comparator_3_lt);
  Adder #(.width(32)) adder_1 (.a(bit_extender_3_out), .b(32'h1), .out(adder_1_out));  // open: cin, cout
  Multiplexer #(.width(32)) multiplexer_1 (
    .in0(bit_extender_4_out), .in1(adder_1_out), .out(multiplexer_1_out), .sel(in_1[15]));  // open: en
  Multiplexer #(.width(32)) multiplexer_2 (
    .in0(multiplexer_1_out), .in1({32{1'b0}}), .out(out_2), .sel(or_2_out));  // open: en

  // Other names for the same wires on the sheet: sign = in_1[15]
endmodule
