// Logisim project grf.circ as structural Verilog: 2 circuits, main circuit grf
module grf (
  input  clk,
  input  reset,
  input  WE,
  input  [4:0] A1,
  input  [4:0] A2,
  input  [4:0] A3,
  input  [31:0] WD,
  output [31:0] RD1,
  output [31:0] RD2
);

  wire and_1_out, and_2_out, and_3_out, and_4_out, and_5_out, and_6_out, and_7_out, and_8_out, and_9_out,
       and_10_out, and_11_out, and_12_out, and_13_out, and_14_out, and_15_out, and_16_out, and_17_out,
       and_18_out, and_19_out, and_20_out, and_21_out, and_22_out, and_23_out, and_24_out, and_25_out,
       and_26_out, and_27_out, and_28_out, and_29_out, and_30_out, and_31_out, and_32_out, decoder_1_out0,
       decoder_1_out1, decoder_1_out2, decoder_2_out0, decoder_2_out1, decoder_2_out2, decoder_2_out3,
       decoder_2_out4, decoder_2_out5, decoder_2_out6, decoder_2_out7;
  wire [31:0] _0, _1, _2, _3, _4, _5, _6, _7, _8, _9, _10, _11, _12, _13, _14, _15, _16, _17, _18, _19, _20,
       _21, _22, _23, _24, _25, _26, _27, _28, _29, _30, _31;

  Decoder #(.select(2)) decoder_1 (
    .out0(decoder_1_out0), .out1(decoder_1_out1), .out2(decoder_1_out2), .sel(A3[4:3]));  // open: out3, en
  and and_1 (and_1_out, WE, decoder_1_out0, decoder_2_out0);
  and and_2 (and_2_out, WE, decoder_1_out1, decoder_2_out0);
  and and_3 (and_3_out, WE, decoder_1_out2, decoder_2_out0);
  and and_4 (and_4_out, WE, decoder_1_out2, decoder_2_out0);
  Register #(.width(32)) register_1 (.D({32{1'b0}}), .en(and_1_out), .Q(_0), .clk(clk), .clr(reset));
  Register #(.width(32)) register_2 (.D(WD), .en(and_2_out), .Q(_8), .clk(clk), .clr(reset));
  Register #(.width(32)) register_3 (.D(WD), .en(and_3_out), .Q(_16), .clk(clk), .clr(reset));
  Register #(.width(32)) register_4 (.D(WD), .en(and_4_out), .Q(_24), .clk(clk), .clr(reset));
  and and_5 (and_5_out, WE, decoder_1_out0, decoder_2_out1);
  and and_6 (and_6_out, WE, decoder_1_out1, decoder_2_out1);
  and and_7 (and_7_out, WE, decoder_1_out2, decoder_2_out1);
  and and_8 (and_8_out, WE, decoder_1_out2, decoder_2_out1);
  Register #(.width(32)) register_5 (.D(WD), .en(and_5_out), .Q(_1), .clk(clk), .clr(reset));
  Register #(.width(32)) register_6 (.D(WD), .en(and_6_out), .Q(_9), .clk(clk), .clr(reset));
  Register #(.width(32)) register_7 (.D(WD), .en(and_7_out), .Q(_17), .clk(clk), .clr(reset));
  Register #(.width(32)) register_8 (.D(WD), .en(and_8_out), .Q(_25), .clk(clk), .clr(reset));
  and and_9 (and_9_out, WE, decoder_1_out0, decoder_2_out2);
  and and_10 (and_10_out, WE, decoder_1_out1, decoder_2_out2);
  and and_11 (and_11_out, WE, decoder_1_out2, decoder_2_out2);
  and and_12 (and_12_out, WE, decoder_1_out2, decoder_2_out2);
  Register #(.width(32)) register_9 (.D(WD), .en(and_9_out), .Q(_2), .clk(clk), .clr(reset));
  Register #(.width(32)) register_10 (.D(WD), .en(and_10_out), .Q(_10), .clk(clk), .clr(reset));
  Register #(.width(32)) register_11 (.D(WD), .en(and_11_out), .Q(_18), .clk(clk), .clr(reset));
  Register #(.width(32)) register_12 (.D(WD), .en(and_12_out), .Q(_26), .clk(clk), .clr(reset));
  and and_13 (and_13_out, WE, decoder_1_out0, decoder_2_out3);
  and and_14 (and_14_out, WE, decoder_1_out1, decoder_2_out3);
  and and_15 (and_15_out, WE, decoder_1_out2, decoder_2_out3);
  Register #(.width(32)) register_13 (.D(WD), .en(and_13_out), .Q(_3), .clk(clk), .clr(reset));
  Register #(.width(32)) register_14 (.D(WD), .en(and_14_out), .Q(_11), .clk(clk), .clr(reset));
  and and_16 (and_16_out, WE, decoder_1_out2, decoder_2_out3);
  Decoder #(.select(3)) decoder_2 (
    .out0(decoder_2_out0), .out1(decoder_2_out1), .out2(decoder_2_out2), .out3(decoder_2_out3),
    .out4(decoder_2_out4), .out5(decoder_2_out5), .out6(decoder_2_out6), .out7(decoder_2_out7), .sel(A3[2:0]));  // open: en
  Register #(.width(32)) register_15 (.D(WD), .en(and_15_out), .Q(_19), .clk(clk), .clr(reset));
  Register #(.width(32)) register_16 (.D(WD), .en(and_16_out), .Q(_27), .clk(clk), .clr(reset));
  and and_17 (and_17_out, WE, decoder_1_out0, decoder_2_out4);
  and and_18 (and_18_out, WE, decoder_1_out1, decoder_2_out4);
  and and_19 (and_19_out, WE, decoder_1_out2, decoder_2_out4);
  and and_20 (and_20_out, WE, decoder_1_out2, decoder_2_out4);
  Register #(.width(32)) register_17 (.D(WD), .en(and_17_out), .Q(_4), .clk(clk), .clr(reset));
  Register #(.width(32)) register_18 (.D(WD), .en(and_18_out), .Q(_12), .clk(clk), .clr(reset));
  Register #(.width(32)) register_19 (.D(WD), .en(and_19_out), .Q(_20), .clk(clk), .clr(reset));
  Register #(.width(32)) register_20 (.D(WD), .en(and_20_out), .Q(_28), .clk(clk), .clr(reset));
  and and_21 (and_21_out, WE, decoder_1_out0, decoder_2_out5);
  and and_22 (and_22_out, WE, decoder_1_out1, decoder_2_out5);
  and and_23 (and_23_out, WE, decoder_1_out2, decoder_2_out5);
  and and_24 (and_24_out, WE, decoder_1_out2, decoder_2_out5);
  Register #(.width(32)) register_21 (.D(WD), .en(and_21_out), .Q(_5), .clk(clk), .clr(reset));
  Register #(.width(32)) register_22 (.D(WD), .en(and_22_out), .Q(_13), .clk(clk), .clr(reset));
  Register #(.width(32)) register_23 (.D(WD), .en(and_23_out), .Q(_21), .clk(clk), .clr(reset));
  Register #(.width(32)) register_24 (.D(WD), .en(and_24_out), .Q(_29), .clk(clk), .clr(reset));
  and and_25 (and_25_out, WE, decoder_1_out0, decoder_2_out6);
  and and_26 (and_26_out, WE, decoder_1_out1, decoder_2_out6);
  and and_27 (and_27_out, WE, decoder_1_out2, decoder_2_out6);
  and and_28 (and_28_out, WE, decoder_1_out2, decoder_2_out6);
  Register #(.width(32)) register_25 (.D(WD), .en(and_25_out), .Q(_6), .clk(clk), .clr(reset));
  Register #(.width(32)) register_26 (.D(WD), .en(and_26_out), .Q(_14), .clk(clk), .clr(reset));
  Register #(.width(32)) register_27 (.D(WD), .en(and_27_out), .Q(_22), .clk(clk), .clr(reset));
  Register #(.width(32)) register_28 (.D(WD), .en(and_28_out), .Q(_30), .clk(clk), .clr(reset));
  and and_29 (and_29_out, WE, decoder_1_out0, decoder_2_out7);
  and and_30 (and_30_out, WE, decoder_1_out1, decoder_2_out7);
  and and_31 (and_31_out, WE, decoder_1_out2, decoder_2_out7);
  and and_32 (and_32_out, WE, decoder_1_out2, decoder_2_out7);
  Register #(.width(32)) register_29 (.D(WD), .en(and_29_out), .Q(_7), .clk(clk), .clr(reset));
  Register #(.width(32)) register_30 (.D(WD), .en(and_30_out), .Q(_15), .clk(clk), .clr(reset));
  Register #(.width(32)) register_31 (.D(WD), .en(and_31_out), .Q(_23), .clk(clk), .clr(reset));
  Register #(.width(32)) register_32 (.D(WD), .en(and_32_out), .Q(_31), .clk(clk), .clr(reset));
  // Probe on RD1
  Multiplexer #(.select(5), .width(32)) multiplexer_1 (
    .in0(_0), .in1(_1), .in2(_2), .in3(_3), .in4(_4), .in5(_5), .in6(_6), .in7(_7), .in8(_8), .in9(_9),
    .in10(_10), .in11(_11), .in12(_12), .in13(_13), .in14(_14), .in15(_15), .in16(_16), .in17(_17),
    .in18(_18), .in19(_19), .in20(_20), .in21(_21), .in22(_22), .in23(_23), .in24(_24), .in25(_25),
    .in26(_26), .in27(_27), .in28(_28), .in29(_29), .in30(_30), .in31(_31), .out(RD1), .sel(A1));  // open: en
  // Probe on RD2
  Multiplexer #(.select(5), .width(32)) multiplexer_2 (
    .in0(_0), .in1(_1), .in2(_2), .in3(_3), .in4(_4), .in5(_5), .in6(_6), .in7(_7), .in8(_8), .in9(_9),
    .in10(_10), .in11(_11), .in12(_12), .in13(_13), .in14(_14), .in15(_15), .in16(_16), .in17(_17),
    .in18(_18), .in19(_19), .in20(_20), .in21(_21), .in22(_22), .in23(_23), .in24(_24), .in25(_25),
    .in26(_26), .in27(_27), .in28(_28), .in29(_29), .in30(_30), .in31(_31), .out(RD2), .sel(A2));  // open: en

  // Other names for the same wires on the sheet: Line[2:0] = A3[2:0]
endmodule

module grfTest (
  input  in_1
);

  wire clock_1_out;
  wire [7:0] counter_1_q;
  wire [15:0] rom_1_data;
  wire [31:0] grf_1_rd1, grf_1_rd2, rom_2_data;

  Clock clock_1 (.out(clock_1_out));
  Counter counter_1 (.Q(counter_1_q), .clk(clock_1_out));  // open: load, D, count, carry, clr
  ROM #(.dataWidth(16)) rom_1 (.addr(counter_1_q), .data(rom_1_data));  // open: sel
  ROM #(.dataWidth(32)) rom_2 (.addr(counter_1_q), .data(rom_2_data));  // open: sel
  grf grf_1 (
    .A1(rom_1_data[4:0]), .A2(rom_1_data[9:5]), .A3(rom_1_data[14:10]), .WD(rom_2_data), .clk(clock_1_out),
    .reset(in_1), .WE(rom_1_data[15]), .RD1(grf_1_rd1), .RD2(grf_1_rd2));
  // Probe on grf_1_rd2
  // Probe on grf_1_rd1
endmodule
