// Logisim project navigation.circ as structural Verilog: 4 circuits, main circuit navigation
module navigation (
  input  [1:0] dir,
  input  clk,
  input  reset,
  output arrive,
  output hit
);

  wire and_1_out, check_out_3, comparator_1_eq, comparator_2_eq, not_1_out, not_2_out, reset_t;
  wire [2:0] move_out_4, move_out_5, multiplexer_1_out, multiplexer_2_out, nx, ny;

  Register #(.width(3)) x (.D(multiplexer_1_out), .Q(nx), .clk(clk), .clr(reset_t));  // open: en
  Register #(.width(3)) y (.D(multiplexer_2_out), .Q(ny), .clk(clk), .clr(reset_t));  // open: en
  // Probe on nx
  // Probe on ny
  or or_1 (reset_t, arrive, reset);
  // Probe on move_out_4
  move move (.in_1(nx), .in_3(ny), .in_2(dir), .out_4(move_out_4), .out_5(move_out_5));
  // Probe on move_out_5
  Comparator #(.width(3), .mode("unsigned")) comparator_1 (
    .a(3'b010), .b(multiplexer_1_out), .eq(comparator_1_eq));  // open: gt, lt
  Comparator #(.width(3), .mode("unsigned")) comparator_2 (
    .a(multiplexer_2_out), .b(3'b001), .eq(comparator_2_eq));  // open: gt, lt
  flag check (.in_1(move_out_4), .in_2(move_out_5), .out_3(check_out_3));
  and and_1 (and_1_out, comparator_1_eq, comparator_2_eq);
  Multiplexer #(.width(3)) multiplexer_1 (
    .in0(nx), .in1(move_out_4), .out(multiplexer_1_out), .sel(not_1_out));  // open: en
  not not_1 (not_1_out, check_out_3);
  Multiplexer #(.width(3)) multiplexer_2 (
    .in0(ny), .in1(move_out_5), .out(multiplexer_2_out), .sel(not_2_out));  // open: en
  not not_2 (not_2_out, check_out_3);
  D_Flip_Flop d_ff_1 (.clk(clk), .D(and_1_out), .Q(arrive), .reset(reset));  // open: Qn, preset, en
  D_Flip_Flop d_ff_2 (.clk(clk), .D(check_out_3), .Q(hit), .reset(reset_t));  // open: Qn, preset, en
endmodule

module move (
  input  [2:0] in_1,
  input  [1:0] in_2,
  input  [2:0] in_3,
  output [2:0] out_4,
  output [2:0] out_5
);

  wire [2:0] adder_1_out, adder_2_out, subtractor_1_out, subtractor_2_out;

  Adder #(.width(3)) adder_1 (.a(in_1), .b(3'b001), .out(adder_1_out));  // open: cin, cout
  Subtractor #(.width(3)) subtractor_1 (.a(in_1), .b(3'b001), .out(subtractor_1_out));  // open: bin, bout
  Subtractor #(.width(3)) subtractor_2 (.a(in_3), .b(3'b001), .out(subtractor_2_out));  // open: bin, bout
  Adder #(.width(3)) adder_2 (.a(in_3), .b(3'b001), .out(adder_2_out));  // open: cin, cout
  Multiplexer #(.select(2), .width(3)) multiplexer_1 (
    .in0(adder_1_out), .in1(in_1), .in2(subtractor_1_out), .in3(in_1), .out(out_4), .sel(in_2));  // open: en
  Multiplexer #(.select(2), .width(3)) multiplexer_2 (
    .in0(in_3), .in1(adder_2_out), .in2(in_3), .in3(subtractor_2_out), .out(out_5), .sel(in_2));  // open: en
endmodule

module flag (
  input  [2:0] in_1,
  input  [2:0] in_2,
  output out_3
);

  wire and_1_out, comparator_1_eq, comparator_2_gt, comparator_3_eq, comparator_3_gt;

  Comparator #(.width(3), .mode("unsigned")) comparator_1 (.a(in_1), .b(3'b000), .eq(comparator_1_eq));  // open: gt, lt
  Comparator #(.width(3), .mode("unsigned")) comparator_2 (.a(in_1), .b(3'b010), .gt(comparator_2_gt));  // open: eq, lt
  Comparator #(.width(3), .mode("unsigned")) comparator_3 (
    .a(in_2), .b(3'b001), .gt(comparator_3_gt), .eq(comparator_3_eq));  // open: lt
  and and_1 (and_1_out, comparator_1_eq, comparator_3_eq);
  or or_1 (out_3, comparator_2_gt, comparator_3_gt, and_1_out);
endmodule

module _123 (
  input  clk,
  input  \input ,
  output out_3
);

  D_Flip_Flop d_ff_1 (.clk(clk), .D(\input ), .Q(out_3));  // open: Qn, preset, en, reset
endmodule
