// Logisim project regularExpression.circ as structural Verilog: 1 circuit, main circuit fsm
module fsm (
  input  CLR,
  input  [1:0] IN,
  output Z
);

  wire clk, decoder_1_out2, equalac, equalb, equalN;
  wire [1:0] multiplexer_1_out, multiplexer_2_out, multiplexer_3_out, multiplexer_4_out, multiplexer_5_out,
       multiplexer_6_out, register_1_q;

  Clock clock_1 (.out(clk));
  Comparator #(.width(2), .mode("unsigned")) comparator_1 (.a(IN), .b(2'b01), .eq(equalb));  // open: gt, lt
  Comparator #(.width(2), .mode("unsigned")) comparator_2 (.a(IN), .b(2'b11), .eq(equalN));  // open: gt, lt
  Multiplexer #(.width(2)) multiplexer_1 (.in0(2'b00), .in1(2'b01), .out(multiplexer_1_out), .sel(equalb));  // open: en
  Multiplexer #(.width(2)) multiplexer_2 (.in0(2'b00), .in1(2'b01), .out(multiplexer_2_out), .sel(equalb));  // open: en
  Multiplexer #(.width(2)) multiplexer_3 (
    .in0(multiplexer_6_out), .in1(2'b00), .out(multiplexer_3_out), .sel(CLR));  // open: en
  Multiplexer #(.width(2)) multiplexer_4 (
    .in0(multiplexer_2_out), .in1(2'b10), .out(multiplexer_4_out), .sel(equalac));  // open: en
  Register #(.width(2)) register_1 (.D(multiplexer_3_out), .Q(register_1_q), .clk(clk));  // open: en, clr
  Multiplexer #(.width(2)) multiplexer_5 (.in0(2'b00), .in1(2'b01), .out(multiplexer_5_out), .sel(equalb));  // open: en
  nor nor_1 (equalac, equalb, equalN);
  Multiplexer #(.select(2), .width(2)) multiplexer_6 (
    .in0(multiplexer_1_out), .in1(multiplexer_4_out), .in2(multiplexer_5_out), .out(multiplexer_6_out),
    .sel(register_1_q));  // open: in3, en
  Decoder #(.select(2)) decoder_1 (.out2(decoder_1_out2), .sel(register_1_q));  // open: out0, out1, out3, en
  and and_1 (Z, decoder_1_out2, equalac);
endmodule
