// Logisim project npu.circ as structural Verilog: 6 circuits, main circuit main
module main (
  input  reset,
  output [31:0] Instr,
  output [31:0] pc,
  output RegWrite,
  output [4:0] RegAddr,
  output [31:0] RegData,
  output MemWrite,
  output [31:0] MemAddr,
  output [31:0] MemData
);

  wire ALUEXT, clk, controller_1_sllmode, jal, jr, logicOut, not_RInstr, signExt_t;
  wire [1:0] RegChoose;
  wire [2:0] ALUOp;
  wire [4:0] multiplexer_1_out, multiplexer_2_out;
  wire [25:0] bit_extender_1_out;
  wire [31:0] adder_1_out, bit_extender_2_out, MemOut, multiplexer_4_out, multiplexer_6_out, reg1,
       shifter_1_out, signExt;

  Clock clock_1 (.out(clk));
  Bit_Extender #(.in_width(32), .out_width(26)) bit_extender_1 (.in(Instr), .out(bit_extender_1_out));
  // Probe on Instr[31:26]
  // Probe on Instr[25:21]
  // Probe on Instr[20:16]
  IFU IFU (
    .LogicOut(logicOut), .clk(clk), .reset(reset), .Instr(Instr), .pc(pc), .signEXT(signExt), .reg1(reg1),
    .jr(jr), .index(bit_extender_1_out), .jal(jal));
  // Probe on Instr[5:0]
  // Probe on Instr[15:0]
  // Probe on Instr[25:21]
  RAM #(.addrWidth(24), .dataWidth(32), .bus("separate")) ram_1 (
    .addr(MemAddr[25:2]), .din(MemData), .data(MemOut), .str(MemWrite), .clk(clk), .clr(reset));  // open: sel, ld
  Multiplexer #(.width(5)) multiplexer_1 (
    .in0(Instr[15:11]), .in1(Instr[20:16]), .out(multiplexer_1_out), .sel(not_RInstr));  // open: en
  Controller controller_1 (
    .func(Instr[5:0]), .opcode(Instr[31:26]), .not_Rinstr(not_RInstr), .ALUOp(ALUOp), .RegWrite(RegWrite),
    .ALUEXT(ALUEXT), .MemWrite(MemWrite), .RegChoose(RegChoose), .signExt(signExt_t),
    .sllMode(controller_1_sllmode), .jr(jr), .jal(jal));
  Multiplexer #(.width(5)) multiplexer_2 (
    .in0(Instr[25:21]), .in1(Instr[20:16]), .out(multiplexer_2_out), .sel(controller_1_sllmode));  // open: en
  assign bit_extender_2_out = {{16{1'b0}}, Instr[15:0]};  // Bit_Extender bit_extender_2
  assign signExt = {{16{Instr[15]}}, Instr[15:0]};  // Bit_Extender bit_extender_3
  Multiplexer #(.width(5)) multiplexer_3 (
    .in0(multiplexer_1_out), .in1({5{1'b1}}), .out(RegAddr), .sel(jal));  // open: en
  Multiplexer #(.width(32)) multiplexer_4 (
    .in0(bit_extender_2_out), .in1(signExt), .out(multiplexer_4_out), .sel(signExt_t));  // open: en
  Adder #(.width(32)) adder_1 (.a(32'h4), .b(pc), .out(adder_1_out));  // open: cin, cout
  Shifter #(.width(32)) shifter_1 (.in(bit_extender_2_out), .\dist (5'b10000), .out(shifter_1_out));
  GRF GRF (
    .A1(multiplexer_2_out), .A2(Instr[20:16]), .Wreg(RegAddr), .wdata(RegData), .RD1(reg1), .RD2(MemData),
    .clk(clk), .reset(reset), .WE(RegWrite));
  Multiplexer #(.select(2), .width(32)) multiplexer_5 (
    .in0(MemAddr), .in1(MemOut), .in2(shifter_1_out), .in3(adder_1_out), .out(RegData), .sel(RegChoose));  // open: en
  Multiplexer #(.width(32)) multiplexer_6 (
    .in0(MemData), .in1(multiplexer_4_out), .out(multiplexer_6_out), .sel(ALUEXT));  // open: en
  ALU ALU (
    .A(reg1), .B(multiplexer_6_out), .\logic (logicOut), .\output (MemAddr), .ALUOp(ALUOp),
    .imm_10_6(Instr[10:6]));
  // Probe on ALUOp
  // Probe on MemAddr
  // Probe on Instr
  // Probe on pc
  // Probe on RegAddr
  // Probe on RegData
  // Probe on MemAddr
  // Probe on MemData

  // Other names for the same wires on the sheet: func[5:0] = Instr[5:0]; imm_10_6[4:0] = Instr[10:6];
  //   ALUout[31:0] = MemAddr; reg2[31:0] = MemData

  // Notes on the sheet:
  //   zeroEXT
  //   signExt
endmodule

module IFU (
  input  [31:0] signEXT,
  input  [31:0] reg1,
  input  LogicOut,
  input  jr,
  input  jal,
  input  clk,
  input  reset,
  input  [25:0] index,
  output [31:0] Instr,
  output [31:0] pc
);

  wire [1:0] multiplexer_1_out, multiplexer_2_out, multiplexer_3_out;
  wire [23:0] bit_extender_2_out;
  wire [27:0] bit_extender_1_out, shifter_2_out;
  wire [31:0] adder_1_out, adder_3_out, multiplexer_4_out, register_1_q, shifter_1_out, subtractor_1_out;

  // Probe on reg1
  Multiplexer #(.width(2)) multiplexer_1 (
    .in0(2'b00), .in1(2'b01), .out(multiplexer_1_out), .sel(LogicOut));  // open: en
  Multiplexer #(.width(2)) multiplexer_2 (
    .in0(multiplexer_1_out), .in1(2'b10), .out(multiplexer_2_out), .sel(jr));  // open: en
  Shifter #(.width(32)) shifter_1 (.in(signEXT), .\dist (5'b00010), .out(shifter_1_out));
  Subtractor #(.width(32)) subtractor_1 (.a(reg1), .b(32'h3000), .out(subtractor_1_out));  // open: bin, bout
  Multiplexer #(.width(2)) multiplexer_3 (
    .in0(multiplexer_2_out), .in1(2'b11), .out(multiplexer_3_out), .sel(jal));  // open: en
  assign bit_extender_1_out = {{2{1'b0}}, index};  // Bit_Extender bit_extender_1
  Shifter #(.width(28)) shifter_2 (.in(bit_extender_1_out), .\dist (5'b00010), .out(shifter_2_out));
  Adder #(.width(32)) adder_1 (.a(adder_3_out), .b(shifter_1_out), .out(adder_1_out));  // open: cin, cout
  Multiplexer #(.select(2), .width(32)) multiplexer_4 (
    .in0(adder_3_out), .in1(adder_1_out), .in2(subtractor_1_out), .in3({pc[31:28], shifter_2_out}),
    .out(multiplexer_4_out), .sel(multiplexer_3_out));  // open: en
  Register #(.width(32)) register_1 (.D(multiplexer_4_out), .Q(register_1_q), .clk(clk), .clr(reset));  // open: en
  Adder #(.width(32)) adder_2 (.a(register_1_q), .b(32'h3000), .out(pc));  // open: cin, cout
  Adder #(.width(32)) adder_3 (.a(32'h4), .b(register_1_q), .out(adder_3_out));  // open: cin, cout
  Bit_Extender #(.in_width(30), .out_width(24)) bit_extender_2 (.in(register_1_q[31:2]), .out(bit_extender_2_out));
  ROM #(.addrWidth(24), .dataWidth(32)) rom_1 (.addr(bit_extender_2_out), .data(Instr));  // open: sel

  // Notes on the sheet:
  //   contents of rom_1 (hex, n*v repeats v):
  //   34113293 340502a0 34162542 34046b61 3404b077 3419c1a0 340d8174 340c57a7 341aa097 3419a6a6 3409b002
  //   3408730c 341b6a5c 3416c1c3 341f90a6 340eeb89 10000029 1fa020 2800008 34003044 3e00008 34143050
  //   1fd020 3400008 34003058 3e00008 341a3064 1f4020 1000008 3400306c 3e00008 34083078 1fa820 2a00008
  //   34003080 3e00008 3415308c 1fb020 2c00008 34003094 3e00008 341630a0 1f8020 2000008 340030a8 3e00008
  //   341030b4 1f6820 1a00008 340030bc 3e00008 340d30c8 1f1020 400008 340030d0 3e00008 340230dc 3e00008
  //   34000019 340f0009 340a0029 3413001c 340b0024 3404001b 3409000f 341b0026 34190031 34050000 34180005
  //   34110011 340c001a 340e0020 3412000f 341f0007 34143050 341a3064 340830e4 341530e4 341630e4 341030b4
  //   340d30c8 340230e4 ac180018 ac190014 ac100020 ac150028 ac000020 ac130004 ac000024 ac0c0000 ac1f0024
  //   ac0a0020 ac16002c ac140010 ac120028 ac13002c ac190020 ac0b002c ac10001c ac110030 ac160010 ac090018
  //   341300a6 341100a6 34130069 34180069 12710006 341f31b0 1c59820 3c1f0000 12780002 341f31c0 341f31c0
  //   3418002e 34110012 341f0003 ad4e003b 0 341f31dc 0 341f31e4 0 341f31ec 341f31ec 341f0004 340c00af
  //   341900af 34180030 34180030 adf9fff7 11990005 341f3210 13180003 341f3218 b3f820 341f321c 3419002f
  //   340c002c 341f0029 3405007c 3419007c 340a003a 340b003a 10b90006 341f3244 8f180000 3c050000 114b0002
  //   341f3254 341f3254 34190000 34050008 341f001e 3419003d 3418003d 2404822 13380004 341f3278 164d822 0
  //   341f3280 341f0027 0 341f3290 3c050000 0 8c8b00a1 341f329c 341f002a 0 18cc822 af2f0024 0 341f32b8
  //   341f32b8 341f0013 340a0095 340e0095 114e0005 341f32d0 8e250036 190022 0 341f32dc 340a0019 340e0022
  //   341f0031 340400c7 341800c7 2609822 8d650064 0 341f3304 10980002 341f330c 341f330c 34040008 3418000e
  //   341f001e 0 341f3324 0 aff8cd3c 8f72008e 341f3330 341f0010 3c1b0000 0 341f3344 8f600050 30a0020
  //   341f334c 341f0009 341900c5 341100c5 ad45009f 3c180000 13310003 341f336c ade000af 341f3370 34190018
  //   3411001f 341f0011 8de0004b ac8c0094 0 ae6b0018 341f3390 341f002d adfb008f 0 30ac020 0 341f33a8
  //   341f002b 8e720080 0 8d930098 16f2020 0 341f33c0 341f0017 8e780068 ae2e009d ad790080 3c1b0000
  //   341f33d8 341f002c 340c001e 340c001e 118c0005 341f33f0 8c80ffff 0 8f2e001c 341f33fc 341f000d 341200c7
  //   340000c7 341200bd 341f00bd 3413003e 3411003e 2799020 12400006 341f3428 125f0004 341f3430 12710002
  //   341f3438 341f3438 341f0002 3405007e 340e007e 3c120000 af3b0060 0 341f3458 10ae0002 341f3460 341f3460
  //   3405000e 340e0025 341f001c 34120037 34180037 0 13b9020 3c0b0000 12580002 341f348c 341f348c 341f0017
  //   340f0081 34110081 340f001d 340f001d 11f10006 341f34ac 11ef0004 341f34b4 ae71005e ad4e0043 341f34bc
  //   34110013 341f0015 34110043 34130043 0 0 0 341f34e0 12330002 341f34e8 341f34e8 341f0012 3412007e
  //   3405007e 0 12450004 341f3504 8e720015 8feacb28 341f350c 34050020 34120013 341f000a 340c0092 340b0092
  //   0 341f352c 118b0005 341f3534 0 341f353c a00020 341f3540 340b0023 340c0008 341f0013 340a009a 3400009a
  //   11400005 341f3560 98c820 af25006c 2695822 341f356c 340a0030 341f0011 3c0e0000 0 0 0 341f3588
  //   341f000a 8df8006b 8dc40020 3c1f0000 8df10027 341f35a0 341f000d 3c1b0000 8d7b008c 0 8d6e0010 341f35b8
  //   341f0006 3c180000 8f130000 3e0d820 8caf0054 341f35d0 3413000e 341f001a 8f78000a af09cf24 ac93ffdf 0
  //   341f35f0 341f35f0 3418000e 341f0026 340a0069 34050069 341f0053 34050053 340e000f 340f000f 11450007
  //   341f361c 8d2b0081 13e50004 341f3628 11cf0002 341f3630 341f3630 340a002f 341f0008 34130031 34050031
  //   12650007 341f364c 0 0 341f3658 0 341f3660 341f3660 341f0026 34130058 34050058 0 12650004 341f367c 0
  //   3c120000 341f3684 341f0020 3404002a 3409002a 3c1b0000 0 0 341f36a4 10890002 341f36ac 341f36ac
  //   341f0005 34110023 34040023 12240006 341f36c4 ae6bffc0 8e2b008d 0 341f36d4 341f36d4 341f0011 340c0051
  //   34130051 ae730047 8d8c0007 11930003 341f36f4 5020 341f36f8 341f0015 340c008a 3409008a 34130005
  //   34050005 11890007 341f3718 0 341f3720 3c1f0000 12650002 341f372c 341f372c 3409000f 340c0017 341f0009
  //   271f820 3ee2022 0 afe50038 341f374c 341f002c 0 0 3c0f0000 8e6b001f 341f3764 341f0015 340f00a7
  //   340e00a7 11ee0005 341f377c ac0a0000 af0f009a ac920047 341f3788 340f001f 340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
endmodule

module GRF (
  input  clk,
  input  reset,
  input  WE,
  input  [4:0] A1,
  input  [4:0] A2,
  input  [4:0] Wreg,
  input  [31:0] wdata,
  output [31:0] RD1,
  output [31:0] RD2
);

  wire and_1_out, and_2_out, and_3_out, and_4_out, and_5_out, and_6_out, and_7_out, and_8_out, and_9_out,
       and_10_out, and_11_out, and_12_out, and_13_out, and_14_out, and_15_out, and_16_out, and_17_out,
       and_18_out, and_19_out, and_20_out, and_21_out, and_22_out, and_23_out, and_24_out, and_25_out,
       and_26_out, and_27_out, and_28_out, and_29_out, and_30_out, and_31_out, and_32_out, decoder_1_out0,
       decoder_1_out1, decoder_1_out2, decoder_1_out3, decoder_2_out0, decoder_2_out1, decoder_2_out2,
       decoder_2_out3, decoder_2_out4, decoder_2_out5, decoder_2_out6, decoder_2_out7;
  wire [31:0] _0, _1, _2, _3, _4, _5, _6, _7, _8, _9, _10, _11, _12, _13, _14, _15, _16, _17, _18, _19, _20,
       _21, _22, _23, _24, _25, _26, _27, _28, _29, _30, _31;

  // Probe on Wreg
  Decoder #(.select(2)) decoder_1 (
    .out0(decoder_1_out0), .out1(decoder_1_out1), .out2(decoder_1_out2), .out3(decoder_1_out3),
    .sel(Wreg[4:3]));  // open: en
  and and_1 (and_1_out, WE, decoder_1_out0, decoder_2_out0);
  and and_2 (and_2_out, WE, decoder_1_out1, decoder_2_out0);
  and and_3 (and_3_out, WE, decoder_1_out2, decoder_2_out0);
  and and_4 (and_4_out, WE, decoder_1_out3, decoder_2_out0);
  Register #(.width(32)) register_1 (.D({32{1'b0}}), .en(and_1_out), .Q(_0), .clk(clk), .clr(reset));
  Register #(.width(32)) register_2 (.D(wdata), .en(and_2_out), .Q(_8), .clk(clk), .clr(reset));
  Register #(.width(32)) register_3 (.D(wdata), .en(and_3_out), .Q(_16), .clk(clk), .clr(reset));
  Register #(.width(32)) register_4 (.D(wdata), .en(and_4_out), .Q(_24), .clk(clk), .clr(reset));
  and and_5 (and_5_out, WE, decoder_1_out0, decoder_2_out1);
  and and_6 (and_6_out, WE, decoder_1_out1, decoder_2_out1);
  and and_7 (and_7_out, WE, decoder_1_out2, decoder_2_out1);
  and and_8 (and_8_out, WE, decoder_1_out3, decoder_2_out1);
  Register #(.width(32)) register_5 (.D(wdata), .en(and_5_out), .Q(_1), .clk(clk), .clr(reset));
  Register #(.width(32)) register_6 (.D(wdata), .en(and_6_out), .Q(_9), .clk(clk), .clr(reset));
  Register #(.width(32)) register_7 (.D(wdata), .en(and_7_out), .Q(_17), .clk(clk), .clr(reset));
  Register #(.width(32)) register_8 (.D(wdata), .en(and_8_out), .Q(_25), .clk(clk), .clr(reset));
  and and_9 (and_9_out, WE, decoder_1_out0, decoder_2_out2);
  and and_10 (and_10_out, WE, decoder_1_out1, decoder_2_out2);
  and and_11 (and_11_out, WE, decoder_1_out2, decoder_2_out2);
  and and_12 (and_12_out, WE, decoder_1_out3, decoder_2_out2);
  Register #(.width(32)) register_9 (.D(wdata), .en(and_9_out), .Q(_2), .clk(clk), .clr(reset));
  Register #(.width(32)) register_10 (.D(wdata), .en(and_10_out), .Q(_10), .clk(clk), .clr(reset));
  Register #(.width(32)) register_11 (.D(wdata), .en(and_11_out), .Q(_18), .clk(clk), .clr(reset));
  Register #(.width(32)) register_12 (.D(wdata), .en(and_12_out), .Q(_26), .clk(clk), .clr(reset));
  and and_13 (and_13_out, WE, decoder_1_out0, decoder_2_out3);
  and and_14 (and_14_out, WE, decoder_1_out1, decoder_2_out3);
  and and_15 (and_15_out, WE, decoder_1_out2, decoder_2_out3);
  Register #(.width(32)) register_13 (.D(wdata), .en(and_13_out), .Q(_3), .clk(clk), .clr(reset));
  Register #(.width(32)) register_14 (.D(wdata), .en(and_14_out), .Q(_11), .clk(clk), .clr(reset));
  and and_16 (and_16_out, WE, decoder_1_out3, decoder_2_out3);
  Decoder #(.select(3)) decoder_2 (
    .out0(decoder_2_out0), .out1(decoder_2_out1), .out2(decoder_2_out2), .out3(decoder_2_out3),
    .out4(decoder_2_out4), .out5(decoder_2_out5), .out6(decoder_2_out6), .out7(decoder_2_out7),
    .sel(Wreg[2:0]));  // open: en
  Register #(.width(32)) register_15 (.D(wdata), .en(and_15_out), .Q(_19), .clk(clk), .clr(reset));
  Register #(.width(32)) register_16 (.D(wdata), .en(and_16_out), .Q(_27), .clk(clk), .clr(reset));
  and and_17 (and_17_out, WE, decoder_1_out0, decoder_2_out4);
  and and_18 (and_18_out, WE, decoder_1_out1, decoder_2_out4);
  and and_19 (and_19_out, WE, decoder_1_out2, decoder_2_out4);
  and and_20 (and_20_out, WE, decoder_1_out3, decoder_2_out4);
  Register #(.width(32)) register_17 (.D(wdata), .en(and_17_out), .Q(_4), .clk(clk), .clr(reset));
  Register #(.width(32)) register_18 (.D(wdata), .en(and_18_out), .Q(_12), .clk(clk), .clr(reset));
  Register #(.width(32)) register_19 (.D(wdata), .en(and_19_out), .Q(_20), .clk(clk), .clr(reset));
  Register #(.width(32)) register_20 (.D(wdata), .en(and_20_out), .Q(_28), .clk(clk), .clr(reset));
  and and_21 (and_21_out, WE, decoder_1_out0, decoder_2_out5);
  and and_22 (and_22_out, WE, decoder_1_out1, decoder_2_out5);
  and and_23 (and_23_out, WE, decoder_1_out2, decoder_2_out5);
  and and_24 (and_24_out, WE, decoder_1_out3, decoder_2_out5);
  Register #(.width(32)) register_21 (.D(wdata), .en(and_21_out), .Q(_5), .clk(clk), .clr(reset));
  Register #(.width(32)) register_22 (.D(wdata), .en(and_22_out), .Q(_13), .clk(clk), .clr(reset));
  Register #(.width(32)) register_23 (.D(wdata), .en(and_23_out), .Q(_21), .clk(clk), .clr(reset));
  Register #(.width(32)) register_24 (.D(wdata), .en(and_24_out), .Q(_29), .clk(clk), .clr(reset));
  and and_25 (and_25_out, WE, decoder_1_out0, decoder_2_out6);
  and and_26 (and_26_out, WE, decoder_1_out1, decoder_2_out6);
  and and_27 (and_27_out, WE, decoder_1_out2, decoder_2_out6);
  and and_28 (and_28_out, WE, decoder_1_out3, decoder_2_out6);
  Register #(.width(32)) register_25 (.D(wdata), .en(and_25_out), .Q(_6), .clk(clk), .clr(reset));
  Register #(.width(32)) register_26 (.D(wdata), .en(and_26_out), .Q(_14), .clk(clk), .clr(reset));
  Register #(.width(32)) register_27 (.D(wdata), .en(and_27_out), .Q(_22), .clk(clk), .clr(reset));
  Register #(.width(32)) register_28 (.D(wdata), .en(and_28_out), .Q(_30), .clk(clk), .clr(reset));
  and and_29 (and_29_out, WE, decoder_1_out0, decoder_2_out7);
  and and_30 (and_30_out, WE, decoder_1_out1, decoder_2_out7);
  and and_31 (and_31_out, WE, decoder_1_out2, decoder_2_out7);
  and and_32 (and_32_out, WE, decoder_1_out3, decoder_2_out7);
  Register #(.width(32)) register_29 (.D(wdata), .en(and_29_out), .Q(_7), .clk(clk), .clr(reset));
  Register #(.width(32)) register_30 (.D(wdata), .en(and_30_out), .Q(_15), .clk(clk), .clr(reset));
  Register #(.width(32)) register_31 (.D(wdata), .en(and_31_out), .Q(_23), .clk(clk), .clr(reset));
  Register #(.width(32)) register_32 (.D(wdata), .en(and_32_out), .Q(_31), .clk(clk), .clr(reset));
  // Probe on RD1
  Multiplexer #(.select(5), .width(32)) multiplexer_1 (
    .in0(_0), .in1(_1), .in2(_2), .in3(_3), .in4(_4), .in5(_5), .in6(_6), .in7(_7), .in8(_8), .in9(_9),
    .in10(_10), .in11(_11), .in12(_12), .in13(_13), .in14(_14), .in15(_15), .in16(_16), .in17(_17),
    .in18(_18), .in19(_19), .in20(_20), .in21(_21), .in22(_22), .in23(_23), .in24(_24), .in25(_25),
    .in26(_26), .in27(_27), .in28(_28), .in29(_29), .in30(_30), .in31(_31), .out(RD1), .sel(A1));  // open: en
  // Probe on RD2
  Multiplexer #(.select(5), .width(32)) multiplexer_2 (
    .in0(_0), .in1(_1), .in2(_2), .in3(_3), .in4(_4), .in5(_5), .in6(_6), .in7(_7), .in8(_8), .in9(_9),
    .in10(_10), .in11(_11), .in12(_12), .in13(_13), .in14(_14), .in15(_15), .in16(_16), .in17(_17),
    .in18(_18), .in19(_19), .in20(_20), .in21(_21), .in22(_22), .in23(_23), .in24(_24), .in25(_25),
    .in26(_26), .in27(_27), .in28(_28), .in29(_29), .in30(_30), .in31(_31), .out(RD2), .sel(A2));  // open: en

  // Other names for the same wires on the sheet: WD[31:0] = wdata; Line[2:0] = Wreg[2:0]

  // Notes on the sheet:
  //   SP
endmodule

module ALU (
  input  [31:0] A,
  input  [2:0] ALUOp,
  input  [31:0] B,
  input  [4:0] imm_10_6,
  output \logic ,
  output [31:0] \output 
);

  wire comparator_1_eq, comparator_1_lt, not_1_out;
  wire [31:0] adder_1_out, and_1_out, multiplexer_1_out, or_1_out, shifter_1_out, subtractor_1_out;

  // Probe on A
  // Probe on B
  Adder #(.width(32)) adder_1 (.a(A), .b(B), .out(adder_1_out));  // open: cin, cout
  Subtractor #(.width(32)) subtractor_1 (.a(A), .b(B), .out(subtractor_1_out));  // open: bin, bout
  assign or_1_out = A | B;  // OR_Gate or_1, 32 bits wide
  Comparator #(.width(32)) comparator_1 (.a(A), .b(B), .eq(comparator_1_eq), .lt(comparator_1_lt));  // open: gt
  Shifter #(.width(32)) shifter_1 (.in(A), .\dist (imm_10_6), .out(shifter_1_out));
  assign and_1_out = A & B;  // AND_Gate and_1, 32 bits wide
  Multiplexer #(.width(32)) multiplexer_1 (
    .in0({32{1'b0}}), .in1(32'h1), .out(multiplexer_1_out), .sel(comparator_1_lt));  // open: en
  not not_1 (not_1_out, comparator_1_eq);
  Multiplexer #(.select(3)) multiplexer_2 (
    .in0(1'b0), .in1(1'b0), .in2(1'b0), .in3(comparator_1_eq), .in4(1'b0), .in5(1'b0), .in6(not_1_out),
    .in7(1'b0), .out(\logic ), .sel(ALUOp));  // open: en
  Multiplexer #(.select(3), .width(32)) multiplexer_3 (
    .in0(adder_1_out), .in1(subtractor_1_out), .in2(or_1_out), .in3({32{1'b0}}), .in4(shifter_1_out),
    .in5(and_1_out), .in6({32{1'b0}}), .in7(multiplexer_1_out), .out(\output ), .sel(ALUOp));  // open: en

  // Notes on the sheet:
  //   add 000
  //   sub 001
  //   or 010
  //   equal 011
  //   sll 100
  //   and 101
  //   notequal 110
  //   slt 111
endmodule

module Controller (
  input  [5:0] func,
  input  [5:0] opcode,
  output not_Rinstr,
  output sllMode,
  output jr,
  output [2:0] ALUOp,
  output RegWrite,
  output ALUEXT,
  output signExt,
  output MemWrite,
  output [1:0] RegChoose,
  output jal
);

  wire _0_out, _1_out, _2_out, _3_out, _4_out, _5_out, andi, beq, bne, chooseALU_out, comparator_1_eq, lui,
       lw, ori, Rdecoder_jr, RInstr;
  wire [1:0] multiplexer_5_out, multiplexer_7_out, multiplexer_8_out;
  wire [2:0] multiplexer_1_out, multiplexer_2_out, multiplexer_3_out, multiplexer_4_out, multiplexer_6_out,
       Rdecoder_aluop;

  not _4 (_4_out, opcode[4]);
  not _5 (_5_out, opcode[5]);
  not _2 (_2_out, opcode[2]);
  not _3 (_3_out, opcode[3]);
  not _0 (_0_out, opcode[0]);
  not _1 (_1_out, opcode[1]);
  Rdecoder Rdecoder (.func(func), .ALUOp(Rdecoder_aluop), .jr(Rdecoder_jr));
  and and_1 (jr, RInstr, Rdecoder_jr);
  and u_RInstr (RInstr, _0_out, _1_out, _2_out, _3_out, _4_out, _5_out);
  and u_ori (ori, _5_out, _4_out, opcode[3], opcode[2], _1_out, opcode[0]);
  and u_lw (lw, opcode[5], _4_out, _3_out, _2_out, opcode[1], opcode[0]);
  and sw (MemWrite, opcode[5], _4_out, opcode[3], _2_out, opcode[1], opcode[0]);
  and u_lui (lui, _5_out, _4_out, opcode[3], opcode[2], opcode[1], opcode[0]);
  and u_beq (beq, _5_out, _4_out, _3_out, opcode[2], _1_out, _0_out);
  and u_jal (jal, _5_out, _4_out, _3_out, _2_out, opcode[1], opcode[0]);
  and u_Andi (andi, _5_out, _4_out, opcode[3], opcode[2], _1_out, _0_out);
  and u_bne (bne, _5_out, _4_out, _3_out, opcode[2], _1_out, opcode[0]);
  // Probe on Rdecoder_aluop
  Multiplexer #(.width(3)) multiplexer_1 (
    .in0(3'b111), .in1(Rdecoder_aluop), .out(multiplexer_1_out), .sel(RInstr));  // open: en
  Comparator #(.width(3)) comparator_1 (.a(Rdecoder_aluop), .b(3'b100), .eq(comparator_1_eq));  // open: gt, lt
  Multiplexer #(.width(3)) multiplexer_2 (
    .in0(multiplexer_1_out), .in1(3'b010), .out(multiplexer_2_out), .sel(ori));  // open: en
  Multiplexer #(.width(3)) multiplexer_3 (
    .in0(multiplexer_2_out), .in1(3'b000), .out(multiplexer_3_out), .sel(signExt));  // open: en
  or DM (signExt, lw, MemWrite);
  or chooseALU (chooseALU_out, RInstr, andi, ori);
  and and_2 (sllMode, comparator_1_eq, RInstr);
  Multiplexer #(.width(3)) multiplexer_4 (
    .in0(multiplexer_3_out), .in1(3'b011), .out(multiplexer_4_out), .sel(beq));  // open: en
  Multiplexer #(.width(2)) multiplexer_5 (
    .in0(2'b11), .in1(2'b00), .out(multiplexer_5_out), .sel(chooseALU_out));  // open: en
  Multiplexer #(.width(3)) multiplexer_6 (
    .in0(multiplexer_4_out), .in1(3'b101), .out(multiplexer_6_out), .sel(andi));  // open: en
  Multiplexer #(.width(2)) multiplexer_7 (
    .in0(multiplexer_5_out), .in1(2'b01), .out(multiplexer_7_out), .sel(lw));  // open: en
  Multiplexer #(.width(2)) multiplexer_8 (
    .in0(multiplexer_7_out), .in1(2'b10), .out(multiplexer_8_out), .sel(lui));  // open: en
  not not_1 (not_Rinstr, RInstr);
  Multiplexer #(.width(3)) multiplexer_9 (.in0(multiplexer_6_out), .in1(3'b110), .out(ALUOp), .sel(bne));  // open: en
  Multiplexer #(.width(2)) multiplexer_10 (
    .in0(multiplexer_8_out), .in1(2'b11), .out(RegChoose), .sel(jal));  // open: en
  or or_1 (RegWrite, RInstr, lui, andi, lw, ori);
  or or_2 (ALUEXT, ori, lw, andi, MemWrite);
endmodule

module Rdecoder (
  input  [5:0] func,
  output [2:0] ALUOp,
  output jr
);

  wire _0_out, _1_out, _2_out, _3_out, _4_out, _5_out, add_2_out, Add_out, Addu_out, And_out, Or_out,
       Sll_out, Slt_out, sub_2_out, Sub_out, Subu_out;
  wire [2:0] multiplexer_1_out, multiplexer_2_out, multiplexer_3_out, multiplexer_4_out, multiplexer_5_out,
       multiplexer_6_out;

  not _5 (_5_out, func[5]);
  not _4 (_4_out, func[4]);
  not _3 (_3_out, func[3]);
  not _2 (_2_out, func[2]);
  not _0 (_0_out, func[0]);
  not _1 (_1_out, func[1]);
  and Add (Add_out, func[5], _4_out, _3_out, _2_out, _1_out, _0_out);
  and Addu (Addu_out, func[5], _4_out, _3_out, _2_out, _1_out, func[0]);
  and Sub (Sub_out, func[5], _4_out, _3_out, _2_out, func[1], _0_out);
  and Subu (Subu_out, func[5], _4_out, _3_out, _2_out, func[1], func[0]);
  and Sll (Sll_out, _5_out, _4_out, _3_out, _2_out, _1_out, _0_out);
  and u_jr (jr, _5_out, _4_out, func[3], _2_out, _1_out, _0_out);
  and And (And_out, func[5], _4_out, _3_out, func[2], _1_out, _0_out);
  and Or (Or_out, func[5], _4_out, _3_out, func[2], _1_out, func[0]);
  and Slt (Slt_out, func[5], _4_out, func[3], _2_out, func[1], _0_out);
  or add_2 (add_2_out, Add_out, Addu_out);
  or sub_2 (sub_2_out, Sub_out, Subu_out);
  Multiplexer #(.width(3)) multiplexer_1 (
    .in0(3'b111), .in1(3'b000), .out(multiplexer_1_out), .sel(add_2_out));  // open: en
  Multiplexer #(.width(3)) multiplexer_2 (
    .in0(multiplexer_1_out), .in1(3'b001), .out(multiplexer_2_out), .sel(sub_2_out));  // open: en
  Multiplexer #(.width(3)) multiplexer_3 (
    .in0(multiplexer_2_out), .in1(3'b100), .out(multiplexer_3_out), .sel(Sll_out));  // open: en
  Multiplexer #(.width(3)) multiplexer_4 (
    .in0(multiplexer_3_out), .in1(3'b000), .out(multiplexer_4_out), .sel(jr));  // open: en
  Multiplexer #(.width(3)) multiplexer_5 (
    .in0(multiplexer_4_out), .in1(3'b101), .out(multiplexer_5_out), .sel(And_out));  // open: en
  Multiplexer #(.width(3)) multiplexer_6 (
    .in0(multiplexer_5_out), .in1(3'b010), .out(multiplexer_6_out), .sel(Or_out));  // open: en
  Multiplexer #(.width(3)) multiplexer_7 (
    .in0(multiplexer_6_out), .in1(3'b111), .out(ALUOp), .sel(Slt_out));  // open: en
endmodule
