// Logisim project test.circ as structural Verilog: 7 circuits, main circuit main
module main (
  input  clk,
  input  reset,
  output [31:0] Instr,
  output [31:0] pc,
  output RegWrite,
  output [4:0] RegAddr,
  output [31:0] RegData,
  output MemWrite,
  output [31:0] MemAddr,
  output [31:0] MemData
);

  wire ALUEXT, logicOut, not_RInstr, signExt_t;
  wire [1:0] RegChoose;
  wire [2:0] ALUOp;
  wire [23:0] bit_extender_1_out;
  wire [31:0] bit_extender_2_out, GRF_rd1, MemOut, multiplexer_2_out, multiplexer_3_out, shifter_1_out,
       shifter_2_out, signExt;

  Shifter #(.width(32)) shifter_1 (.in(signExt), .\dist (5'b00010), .out(shifter_1_out));
  // Probe on Instr[31:26]
  // Probe on Instr[25:21]
  // Probe on Instr[20:16]
  // Probe on Instr[15:11]
  IFU ifu_1 (.wdata(shifter_1_out), .WE(logicOut), .clk(clk), .reset(reset), .Instr(Instr), .pc(pc));
  // Probe on Instr[5:0]
  // Probe on Instr[15:0]
  Bit_Extender #(.in_width(30), .out_width(24)) bit_extender_1 (.in(MemAddr[31:2]), .out(bit_extender_1_out));
  Controller controller_1 (
    .opcode(Instr[31:26]), .func(Instr[5:0]), .signExt(signExt_t), .not_Rinstr(not_RInstr), .ALUOp(ALUOp),
    .RegWrite(RegWrite), .ALUEXT(ALUEXT), .MemWrite(MemWrite), .RegChoose(RegChoose));
  Multiplexer #(.width(5)) multiplexer_1 (
    .in0(Instr[15:11]), .in1(Instr[20:16]), .out(RegAddr), .sel(not_RInstr));  // open: en
  RAM #(.addrWidth(24), .dataWidth(32), .bus("separate")) ram_1 (
    .addr(bit_extender_1_out), .din(MemData), .data(MemOut), .str(MemWrite), .clk(clk), .clr(reset));  // open: sel, ld
  assign bit_extender_2_out = {{16{1'b0}}, Instr[15:0]};  // Bit_Extender bit_extender_2
  assign signExt = {{16{Instr[15]}}, Instr[15:0]};  // Bit_Extender bit_extender_3
  GRF GRF (
    .A1(Instr[25:21]), .A2(Instr[20:16]), .Wreg(RegAddr), .wdata(RegData), .RD1(GRF_rd1), .RD2(MemData),
    .clk(clk), .reset(reset), .WE(RegWrite));
  Multiplexer #(.width(32)) multiplexer_2 (
    .in0(bit_extender_2_out), .in1(signExt), .out(multiplexer_2_out), .sel(signExt_t));  // open: en
  Multiplexer #(.width(32)) multiplexer_3 (
    .in0(MemData), .in1(multiplexer_2_out), .out(multiplexer_3_out), .sel(ALUEXT));  // open: en
  Shifter #(.width(32)) shifter_2 (.in(bit_extender_2_out), .\dist (5'b10000), .out(shifter_2_out));
  Multiplexer #(.select(2), .width(32)) multiplexer_4 (
    .in0(MemAddr), .in1(MemOut), .in2(shifter_2_out), .in3({32{1'b0}}), .out(RegData), .sel(RegChoose));  // open: en
  ALU ALU (.A(GRF_rd1), .B(multiplexer_3_out), .\logic (logicOut), .\output (MemAddr), .ALUOp(ALUOp));
  // Probe on RegChoose
  // Probe on Instr
  // Probe on pc
  // Probe on RegAddr
  // Probe on RegData
  // Probe on MemAddr
  // Probe on MemData

  // Other names for the same wires on the sheet: func[5:0] = Instr[5:0]; ALUout[31:0] = MemAddr

  // Notes on the sheet:
  //   zeroEXT
  //   signExt
endmodule

module IFU (
  input  [31:0] wdata,
  input  WE,
  input  clk,
  input  reset,
  output [31:0] Instr,
  output [31:0] pc
);

  wire [23:0] bit_extender_1_out;
  wire [31:0] adder_1_out, adder_2_out, multiplexer_1_out, register_1_q;

  Adder #(.width(32)) adder_1 (.a(adder_2_out), .b(wdata), .out(adder_1_out));  // open: cin, cout
  Multiplexer #(.width(32)) multiplexer_1 (
    .in0(adder_2_out), .in1(adder_1_out), .out(multiplexer_1_out), .sel(WE));  // open: en
  Register #(.width(32)) register_1 (.D(multiplexer_1_out), .Q(register_1_q), .clk(clk), .clr(reset));  // open: en
  Adder #(.width(32)) adder_2 (.a(32'h4), .b(register_1_q), .out(adder_2_out));  // open: cin, cout
  Bit_Extender #(.in_width(30), .out_width(24)) bit_extender_1 (.in(register_1_q[31:2]), .out(bit_extender_1_out));
  Adder #(.width(32)) adder_3 (.a(register_1_q), .b(32'h3000), .out(pc));  // open: cin, cout
  ROM #(.addrWidth(24), .dataWidth(32)) rom_1 (.addr(bit_extender_1_out), .data(Instr));  // open: sel

  // Notes on the sheet:
  //   contents of rom_1 (hex, n*v repeats v):
  //   34000048 34010001 34020002 34030003 34040004 34050005 34060006 34070007 34080008 34090009 340a000a
  //   340b000b 340c000c 340d000d 340e000e 340f000f 34100010 34110011 34120012 34130013 34140014 34150015
  //   34160016 34170017 34180018 34190019 341a001a 341b001b 341c001c 341d001d 341e001e 341f001f 3c09ffff
  //   3549ffff 341d0000 111f000b 2538822 10e9820 354b03e8 3c04abcd 0 afa80000 3a4e820 8fb2fffc 0 1014020
  //   1000fff4 0 3c070064
endmodule

module GRF (
  input  clk,
  input  reset,
  input  WE,
  input  [4:0] A1,
  input  [4:0] A2,
  input  [4:0] Wreg,
  input  [31:0] wdata,
  output [31:0] RD1,
  output [31:0] RD2
);

  wire and_1_out, and_2_out, and_3_out, and_4_out, and_5_out, and_6_out, and_7_out, and_8_out, and_9_out,
       and_10_out, and_11_out, and_12_out, and_13_out, and_14_out, and_15_out, and_16_out, and_17_out,
       and_18_out, and_19_out, and_20_out, and_21_out, and_22_out, and_23_out, and_24_out, and_25_out,
       and_26_out, and_27_out, and_28_out, and_29_out, and_30_out, and_31_out, and_32_out, decoder_1_out0,
       decoder_1_out1, decoder_1_out2, decoder_1_out3, decoder_2_out0, decoder_2_out1, decoder_2_out2,
       decoder_2_out3, decoder_2_out4, decoder_2_out5, decoder_2_out6, decoder_2_out7;
  wire [31:0] _0, _1, _2, _3, _4, _5, _6, _7, _8, _9, _10, _11, _12, _13, _14, _15, _16, _17, _18, _19, _20,
       _21, _22, _23, _24, _25, _26, _27, _28, _29, _30, _31;

  // Probe on Wreg
  Decoder #(.select(2)) decoder_1 (
    .out0(decoder_1_out0), .out1(decoder_1_out1), .out2(decoder_1_out2), .out3(decoder_1_out3),
    .sel(Wreg[4:3]));  // open: en
  and and_1 (and_1_out, WE, decoder_1_out0, decoder_2_out0);
  and and_2 (and_2_out, WE, decoder_1_out1, decoder_2_out0);
  and and_3 (and_3_out, WE, decoder_1_out2, decoder_2_out0);
  and and_4 (and_4_out, WE, decoder_1_out3, decoder_2_out0);
  Register #(.width(32)) register_1 (.D({32{1'b0}}), .en(and_1_out), .Q(_0), .clk(clk), .clr(reset));
  Register #(.width(32)) register_2 (.D(wdata), .en(and_2_out), .Q(_8), .clk(clk), .clr(reset));
  Register #(.width(32)) register_3 (.D(wdata), .en(and_3_out), .Q(_16), .clk(clk), .clr(reset));
  Register #(.width(32)) register_4 (.D(wdata), .en(and_4_out), .Q(_24), .clk(clk), .clr(reset));
  and and_5 (and_5_out, WE, decoder_1_out0, decoder_2_out1);
  and and_6 (and_6_out, WE, decoder_1_out1, decoder_2_out1);
  and and_7 (and_7_out, WE, decoder_1_out2, decoder_2_out1);
  and and_8 (and_8_out, WE, decoder_1_out3, decoder_2_out1);
  Register #(.width(32)) register_5 (.D(wdata), .en(and_5_out), .Q(_1), .clk(clk), .clr(reset));
  Register #(.width(32)) register_6 (.D(wdata), .en(and_6_out), .Q(_9), .clk(clk), .clr(reset));
  Register #(.width(32)) register_7 (.D(wdata), .en(and_7_out), .Q(_17), .clk(clk), .clr(reset));
  Register #(.width(32)) register_8 (.D(wdata), .en(and_8_out), .Q(_25), .clk(clk), .clr(reset));
  and and_9 (and_9_out, WE, decoder_1_out0, decoder_2_out2);
  and and_10 (and_10_out, WE, decoder_1_out1, decoder_2_out2);
  and and_11 (and_11_out, WE, decoder_1_out2, decoder_2_out2);
  and and_12 (and_12_out, WE, decoder_1_out3, decoder_2_out2);
  Register #(.width(32)) register_9 (.D(wdata), .en(and_9_out), .Q(_2), .clk(clk), .clr(reset));
  Register #(.width(32)) register_10 (.D(wdata), .en(and_10_out), .Q(_10), .clk(clk), .clr(reset));
  Register #(.width(32)) register_11 (.D(wdata), .en(and_11_out), .Q(_18), .clk(clk), .clr(reset));
  Register #(.width(32)) register_12 (.D(wdata), .en(and_12_out), .Q(_26), .clk(clk), .clr(reset));
  and and_13 (and_13_out, WE, decoder_1_out0, decoder_2_out3);
  and and_14 (and_14_out, WE, decoder_1_out1, decoder_2_out3);
  and and_15 (and_15_out, WE, decoder_1_out2, decoder_2_out3);
  Register #(.width(32)) register_13 (.D(wdata), .en(and_13_out), .Q(_3), .clk(clk), .clr(reset));
  Register #(.width(32)) register_14 (.D(wdata), .en(and_14_out), .Q(_11), .clk(clk), .clr(reset));
  and and_16 (and_16_out, WE, decoder_1_out3, decoder_2_out3);
  Decoder #(.select(3)) decoder_2 (
    .out0(decoder_2_out0), .out1(decoder_2_out1), .out2(decoder_2_out2), .out3(decoder_2_out3),
    .out4(decoder_2_out4), .out5(decoder_2_out5), .out6(decoder_2_out6), .out7(decoder_2_out7),
    .sel(Wreg[2:0]));  // open: en
  Register #(.width(32)) register_15 (.D(wdata), .en(and_15_out), .Q(_19), .clk(clk), .clr(reset));
  Register #(.width(32)) register_16 (.D(wdata), .en(and_16_out), .Q(_27), .clk(clk), .clr(reset));
  and and_17 (and_17_out, WE, decoder_1_out0, decoder_2_out4);
  and and_18 (and_18_out, WE, decoder_1_out1, decoder_2_out4);
  and and_19 (and_19_out, WE, decoder_1_out2, decoder_2_out4);
  and and_20 (and_20_out, WE, decoder_1_out3, decoder_2_out4);
  Register #(.width(32)) register_17 (.D(wdata), .en(and_17_out), .Q(_4), .clk(clk), .clr(reset));
  Register #(.width(32)) register_18 (.D(wdata), .en(and_18_out), .Q(_12), .clk(clk), .clr(reset));
  Register #(.width(32)) register_19 (.D(wdata), .en(and_19_out), .Q(_20), .clk(clk), .clr(reset));
  Register #(.width(32)) register_20 (.D(wdata), .en(and_20_out), .Q(_28), .clk(clk), .clr(reset));
  and and_21 (and_21_out, WE, decoder_1_out0, decoder_2_out5);
  and and_22 (and_22_out, WE, decoder_1_out1, decoder_2_out5);
  and and_23 (and_23_out, WE, decoder_1_out2, decoder_2_out5);
  and and_24 (and_24_out, WE, decoder_1_out3, decoder_2_out5);
  Register #(.width(32)) register_21 (.D(wdata), .en(and_21_out), .Q(_5), .clk(clk), .clr(reset));
  Register #(.width(32)) register_22 (.D(wdata), .en(and_22_out), .Q(_13), .clk(clk), .clr(reset));
  Register #(.width(32)) register_23 (.D(wdata), .en(and_23_out), .Q(_21), .clk(clk), .clr(reset));
  Register #(.width(32)) register_24 (.D(wdata), .en(and_24_out), .Q(_29), .clk(clk), .clr(reset));
  and and_25 (and_25_out, WE, decoder_1_out0, decoder_2_out6);
  and and_26 (and_26_out, WE, decoder_1_out1, decoder_2_out6);
  and and_27 (and_27_out, WE, decoder_1_out2, decoder_2_out6);
  and and_28 (and_28_out, WE, decoder_1_out3, decoder_2_out6);
  Register #(.width(32)) register_25 (.D(wdata), .en(and_25_out), .Q(_6), .clk(clk), .clr(reset));
  Register #(.width(32)) register_26 (.D(wdata), .en(and_26_out), .Q(_14), .clk(clk), .clr(reset));
  Register #(.width(32)) register_27 (.D(wdata), .en(and_27_out), .Q(_22), .clk(clk), .clr(reset));
  Register #(.width(32)) register_28 (.D(wdata), .en(and_28_out), .Q(_30), .clk(clk), .clr(reset));
  and and_29 (and_29_out, WE, decoder_1_out0, decoder_2_out7);
  and and_30 (and_30_out, WE, decoder_1_out1, decoder_2_out7);
  and and_31 (and_31_out, WE, decoder_1_out2, decoder_2_out7);
  and and_32 (and_32_out, WE, decoder_1_out3, decoder_2_out7);
  Register #(.width(32)) register_29 (.D(wdata), .en(and_29_out), .Q(_7), .clk(clk), .clr(reset));
  Register #(.width(32)) register_30 (.D(wdata), .en(and_30_out), .Q(_15), .clk(clk), .clr(reset));
  Register #(.width(32)) register_31 (.D(wdata), .en(and_31_out), .Q(_23), .clk(clk), .clr(reset));
  Register #(.width(32)) register_32 (.D(wdata), .en(and_32_out), .Q(_31), .clk(clk), .clr(reset));
  // Probe on RD1
  Multiplexer #(.select(5), .width(32)) multiplexer_1 (
    .in0(_0), .in1(_1), .in2(_2), .in3(_3), .in4(_4), .in5(_5), .in6(_6), .in7(_7), .in8(_8), .in9(_9),
    .in10(_10), .in11(_11), .in12(_12), .in13(_13), .in14(_14), .in15(_15), .in16(_16), .in17(_17),
    .in18(_18), .in19(_19), .in20(_20), .in21(_21), .in22(_22), .in23(_23), .in24(_24), .in25(_25),
    .in26(_26), .in27(_27), .in28(_28), .in29(_29), .in30(_30), .in31(_31), .out(RD1), .sel(A1));  // open: en
  // Probe on RD2
  Multiplexer #(.select(5), .width(32)) multiplexer_2 (
    .in0(_0), .in1(_1), .in2(_2), .in3(_3), .in4(_4), .in5(_5), .in6(_6), .in7(_7), .in8(_8), .in9(_9),
    .in10(_10), .in11(_11), .in12(_12), .in13(_13), .in14(_14), .in15(_15), .in16(_16), .in17(_17),
    .in18(_18), .in19(_19), .in20(_20), .in21(_21), .in22(_22), .in23(_23), .in24(_24), .in25(_25),
    .in26(_26), .in27(_27), .in28(_28), .in29(_29), .in30(_30), .in31(_31), .out(RD2), .sel(A2));  // open: en

  // Other names for the same wires on the sheet: WD[31:0] = wdata; Line[2:0] = Wreg[2:0]
endmodule

module ALU (
  input  [31:0] A,
  input  [2:0] ALUOp,
  input  [31:0] B,
  output \logic ,
  output [31:0] \output 
);

  wire comparator_1_eq;
  wire [31:0] adder_1_out, or_1_out, subtractor_1_out;

  Adder #(.width(32)) adder_1 (.a(A), .b(B), .out(adder_1_out));  // open: cin, cout
  Subtractor #(.width(32)) subtractor_1 (.a(A), .b(B), .out(subtractor_1_out));  // open: bin, bout
  assign or_1_out = A | B;  // OR_Gate or_1, 32 bits wide
  Comparator #(.width(32)) comparator_1 (.a(A), .b(B), .eq(comparator_1_eq));  // open: gt, lt
  Multiplexer #(.select(3)) multiplexer_1 (
    .in0(1'b0), .in1(1'b0), .in2(1'b0), .in3(comparator_1_eq), .in4(1'b0), .in5(1'b0), .in6(1'b0),
    .in7(1'b0), .out(\logic ), .sel(ALUOp));  // open: en
  Multiplexer #(.select(3), .width(32)) multiplexer_2 (
    .in0(adder_1_out), .in1(subtractor_1_out), .in2(or_1_out), .in3({32{1'b0}}), .in4({32{1'b0}}),
    .in5({32{1'b0}}), .in6({32{1'b0}}), .in7({32{1'b0}}), .out(\output ), .sel(ALUOp));  // open: en
endmodule

module Controller (
  input  [5:0] opcode,
  input  [5:0] func,
  output not_Rinstr,
  output [2:0] ALUOp,
  output RegWrite,
  output ALUEXT,
  output signExt,
  output MemWrite,
  output [1:0] RegChoose
);

  wire _0_out, _1_out, _2_out, _3_out, _4_out, _5_out, beq, chooseALU_out, lui, lw, ori, RInstr;
  wire [1:0] multiplexer_5_out, multiplexer_6_out;
  wire [2:0] multiplexer_1_out, multiplexer_2_out, multiplexer_3_out, Rdecoder_aluop;

  not _5 (_5_out, opcode[5]);
  not _4 (_4_out, opcode[4]);
  not _2 (_2_out, opcode[2]);
  not _3 (_3_out, opcode[3]);
  not _1 (_1_out, opcode[1]);
  not _0 (_0_out, opcode[0]);
  and u_RInstr (RInstr, _0_out, _1_out, _2_out, _3_out, _4_out, _5_out);
  and u_ori (ori, _5_out, _4_out, opcode[3], opcode[2], _1_out, opcode[0]);
  and u_lw (lw, opcode[5], _4_out, _3_out, _2_out, opcode[1], opcode[0]);
  and sw (MemWrite, opcode[5], _4_out, opcode[3], _2_out, opcode[1], opcode[0]);
  and u_lui (lui, _5_out, _4_out, opcode[3], opcode[2], opcode[1], opcode[0]);
  and u_beq (beq, _5_out, _4_out, _3_out, opcode[2], _1_out, _0_out);
  // AND_Gate nop has open pins: in0=_5_out, in1=_4_out, in2=_3_out, in3=_2_out, in4=_1_out, in5=_0_out, out=open
  Rdecoder Rdecoder (.func(func), .ALUOp(Rdecoder_aluop));
  Multiplexer #(.width(3)) multiplexer_1 (
    .in0(3'b111), .in1(Rdecoder_aluop), .out(multiplexer_1_out), .sel(RInstr));  // open: en
  Multiplexer #(.width(3)) multiplexer_2 (
    .in0(multiplexer_1_out), .in1(3'b010), .out(multiplexer_2_out), .sel(ori));  // open: en
  Multiplexer #(.width(3)) multiplexer_3 (
    .in0(multiplexer_2_out), .in1(3'b000), .out(multiplexer_3_out), .sel(signExt));  // open: en
  or DM (signExt, lw, MemWrite);
  or chooseALU (chooseALU_out, RInstr, ori);
  Multiplexer #(.width(3)) multiplexer_4 (.in0(multiplexer_3_out), .in1(3'b011), .out(ALUOp), .sel(beq));  // open: en
  Multiplexer #(.width(2)) multiplexer_5 (
    .in0(2'b11), .in1(2'b00), .out(multiplexer_5_out), .sel(chooseALU_out));  // open: en
  Multiplexer #(.width(2)) multiplexer_6 (
    .in0(multiplexer_5_out), .in1(2'b01), .out(multiplexer_6_out), .sel(lw));  // open: en
  or or_1 (RegWrite, RInstr, lui, lw, ori);
  Multiplexer #(.width(2)) multiplexer_7 (
    .in0(multiplexer_6_out), .in1(2'b10), .out(RegChoose), .sel(lui));  // open: en
  not not_1 (not_Rinstr, RInstr);
  or or_2 (ALUEXT, ori, lw, MemWrite);
endmodule

module Rdecoder (
  input  [5:0] func,
  output [2:0] ALUOp
);

  wire _0_out, _1_out, _2_out, _3_out, _4_out, _5_out;
  wire [1:0] Add_out;

  not _4 (_4_out, func[4]);
  not _5 (_5_out, func[5]);
  not _3 (_3_out, func[3]);
  not _2 (_2_out, func[2]);
  not _0 (_0_out, func[0]);
  not _1 (_1_out, func[1]);
  and Add (Add_out[0], _0_out, _1_out, _2_out, _3_out, _4_out, func[5]);
  and Sub (Add_out[1], func[5], _4_out, _3_out, _2_out, func[1], _0_out);
  Multiplexer #(.select(2), .width(3)) multiplexer_1 (
    .in0(3'b111), .in1(3'b000), .in2(3'b001), .in3(3'b111), .out(ALUOp), .sel(Add_out));  // open: en
endmodule

module test (
  input  reset
);

  wire clk, main_1_memwrite, main_1_regwrite;
  wire [4:0] main_1_regaddr;
  wire [23:0] counter_1_q;
  wire [31:0] main_1_instr, main_1_memaddr, main_1_memdata, main_1_pc, main_1_regdata;

  Clock clock_1 (.out(clk));
  Counter #(.width(24), .max('hffffff)) counter_1 (
    .Q(counter_1_q), .clk(clk), .clr(reset));  // open: load, D, count, carry
  main main_1 (
    .clk(reset), .reset(clk), .Instr(main_1_instr), .pc(main_1_pc), .RegWrite(main_1_regwrite),
    .RegAddr(main_1_regaddr), .RegData(main_1_regdata), .MemWrite(main_1_memwrite), .MemAddr(main_1_memaddr),
    .MemData(main_1_memdata));
  RAM #(.addrWidth(24), .dataWidth(32), .bus("separate")) ram_1 (
    .addr(counter_1_q), .din(main_1_instr), .clk(clk), .clr(reset));  // open: data, str, sel, ld
  RAM #(.addrWidth(24), .dataWidth(32), .bus("separate")) ram_2 (
    .addr(counter_1_q), .din(main_1_pc), .clk(clk), .clr(reset));  // open: data, str, sel, ld
  RAM #(.addrWidth(24), .dataWidth(1), .bus("separate")) ram_3 (
    .din(main_1_regwrite), .clk(clk), .clr(reset));  // open: addr, data, str, sel, ld
  RAM #(.addrWidth(24), .dataWidth(5), .bus("separate")) ram_4 (
    .addr(counter_1_q), .din(main_1_regaddr), .clk(clk), .clr(reset));  // open: data, str, sel, ld
  RAM #(.addrWidth(24), .dataWidth(32), .bus("separate")) ram_5 (
    .addr(counter_1_q), .din(main_1_regdata), .clk(clk), .clr(reset));  // open: data, str, sel, ld
  RAM #(.addrWidth(24), .dataWidth(1), .bus("separate")) ram_6 (
    .addr(counter_1_q), .din(main_1_memwrite), .clk(clk), .clr(reset));  // open: data, str, sel, ld
  RAM #(.addrWidth(24), .dataWidth(32), .bus("separate")) ram_7 (
    .addr(counter_1_q), .din(main_1_memaddr), .clk(clk), .clr(reset));  // open: data, str, sel, ld
  RAM #(.addrWidth(24), .dataWidth(32), .bus("separate")) ram_8 (
    .addr(counter_1_q), .din(main_1_memdata), .clk(clk), .clr(reset));  // open: data, str, sel, ld

  // Notes on the sheet:
  //   RegAdr
  //   RegData
  //   MemAdr
  //   MemAdr
  //   Instr
  //   pc
  //   RegWrite
  //   MemWrite
endmodule
