// Logisim project Single-cycle.circ as structural Verilog: 1 circuit, main circuit main
module main (
);

  wire [31:0] adder_1_out, multiplexer_1_out, PC_q;

  Clock clock_1 ();  // open: out
  Register #(.width(32)) PC (.D(multiplexer_1_out), .Q(PC_q));  // open: en, clk, clr
  Multiplexer #(.width(32)) multiplexer_1 (.in0(adder_1_out), .out(multiplexer_1_out));  // open: in1, sel, en
  Adder #(.width(32)) adder_1 (.a(32'h4), .b(PC_q), .out(adder_1_out));  // open: cin, cout
  ROM #(.addrWidth(24), .dataWidth(32)) rom_1 ();  // open: addr, data, sel
endmodule
